# Fritzing sketch Lichtsignal-DCC (saved by Fritzing 0.9.4)
breadboards: 2

parts:
  IC1 = Arduino Nano (Rev3.0)
  HP2 = Pushbutton [package="[THT]"]
  HP0_SH1 = Pushbutton [package="[THT]"]
  HP1 = Pushbutton [package="[THT]"]
  HP0 = Pushbutton [package="[THT]"]
  R1 = Resistor [tolerance=±5% resistance=1.2k package=THT]
  RED_1 = LED - 5mm [color="Red (633nm)" package="5 mm [THT]"]
  Red_2 = LED - 5mm [color="Red (633nm)" package="5 mm [THT]"]
  Green = LED - 5mm [color="Green (570nm)" package="5 mm [THT]"]
  R3 = Resistor [tolerance=±5% resistance=15k package=THT]
  R4 = Resistor [tolerance=±5% resistance=1.2k package=THT]
  R5 = Resistor [tolerance=±5% resistance=1.2k package=THT]
  R6 = Resistor [tolerance=±5% resistance=1.2k package=THT]
  Yellow = LED - 5mm [color="Yellow (585nm)" package="5 mm [THT]"]
  White = LED - 5mm [color="White (6500K)" package="5 mm [THT]"]
  IC2 = 6N136 [package=THT]
  R7 = Resistor [tolerance=±5% resistance=2.2k package=THT]
  D1 = Rectifier Diode [part_number=1N4001 package="300 mil [THT]"]
  R8 = Resistor [tolerance=±5% resistance=1.8k package=THT]
  C1 = Ceramic Capacitor [capacitance=100nF package="100 mil [THT, multilayer]"]
  J1 = Camdenboss CTB0158-2 [part_number="DCC in" package=THT]
  U1 = LTV-817 [package=THT]
  D2 = Rectifier Diode [part_number=1N4001 package="300 mil [THT]"]
  D3 = Rectifier Diode [part_number=1N4001 package="300 mil [THT]"]
  D4 = Rectifier Diode [part_number=1N4001 package="300 mil [THT]"]
  D5 = Rectifier Diode [part_number=1N4001 package="300 mil [THT]"]
  Q1 = PNP-Transistor [package="TO92 [THT]"]
  R9 = Resistor [tolerance=±5% resistance=560 package=THT]

nets:
  N1: IC1.GND, HP2.Pin_3, HP2.Pin_4, HP0_SH1.Pin_3, HP0_SH1.Pin_4, HP1.Pin_3, HP1.Pin_4, HP0.Pin_3, HP0.Pin_4, IC2.B, C1.1, U1.Pin_2
  N2: IC1.D3, HP0.Pin_1, HP0.Pin_2
  N3: IC1.D4, HP1.Pin_1, HP1.Pin_2
  N4: IC1.D5, HP2.Pin_1, HP2.Pin_2
  N5: IC1.D6, HP0_SH1.Pin_1, HP0_SH1.Pin_2
  N6: IC1.D7, R1.Pin_0
  N7: IC1.D8, R4.Pin_0
  N8: IC1.D9, R5.Pin_0
  N9: IC1.D10, R6.Pin_0
  N10: IC1.D11/MOSI, R3.Pin_0
  N11: IC1.D12/MISO, U1.Pin_1
  5V: IC1.5V, RED_1.anode, Red_2.anode, Green.anode, Yellow.anode, White.anode, IC2.Vcc, R7.Pin_0, C1.0
  N12: R1.Pin_1, RED_1.cathode
  N13: Red_2.cathode, R4.Pin_1
  N14: Green.cathode, R5.Pin_1
  N15: R3.Pin_1, White.cathode
  N16: R6.Pin_1, Yellow.cathode
  N17: IC2.A, D1.cathode, R8.Pin_1
  N18: IC2.C#2, D1.anode, J1.pin2, D3.cathode, D5.anode
  N19: IC2.C#5, R7.Pin_1
  N20: R8.Pin_0, J1.pin1, D2.cathode, D4.anode
  N21: U1.Pin_4, D2.anode, D3.anode, Q1.C
  N22: U1.Pin_3, Q1.B
  N23: D4.cathode, D5.cathode, R9.Pin_1
  N24: Q1.E, R9.Pin_0

custom parts:
  6N136: Vishay Semiconductors
  LTV-817: Optocoupler (without sensititvity pins)
